# Fritzing sketch Safe (saved by Fritzing 0.9.0b)
breadboards: 2

parts:
  R1 = Resistor [tolerance=±5% resistance=220 package=THT]
  R2 = Resistor [tolerance=±5% resistance=220 package=THT]
  R3 = Resistor [tolerance=±5% resistance=220 package=THT]
  LED1 = RGB LED (com. cathode, rbg) [package="5 mm [THT]"]
  kEYPAD_MATRICIAL_1 = KEYPAD 4x3
  R4 = Resistor [tolerance=±5% resistance=10k package=THT]
  R5 = Resistor [tolerance=±5% resistance=10k package=THT]
  R6 = Resistor [tolerance=±5% resistance=10k package=THT]
  R7 = Resistor [tolerance=±5% resistance=10k package=THT]
  U2 = mystery part, 8 pins [chip_label=MicroSD spacing=300mil]
  U3 = mystery part, 8 pins [chip_label="RF Receiver" spacing=300mil]
  U4 = mystery part, 4 pins [chip_label="RF Transmitter" spacing=300mil]  # not connected
  J1 = Basic Servo
  U1 = Arduino Mega 2560 (Rev3)
  Arduino1 = Arduino Uno (Rev3)

nets:
  N1: R1.Pin_0, LED1.red_anode
  N2: R2.Pin_0, LED1.blue_anode
  N3: R3.Pin_0, LED1.green_anode
  N4: LED1.common_cathode, R4.Pin_1, R5.Pin_1, R6.Pin_1, R7.Pin_1
  N5: kEYPAD_MATRICIAL_1.col2, R7.Pin_0, Arduino1.D2
  N6: kEYPAD_MATRICIAL_1.arrow2, Arduino1.D8
  N7: kEYPAD_MATRICIAL_1.col3, R6.Pin_0, Arduino1.D4
  N8: kEYPAD_MATRICIAL_1.arrow3, R5.Pin_0
  N9: kEYPAD_MATRICIAL_1.arrow4, R4.Pin_0, Arduino1.D7
  GND: U2.pin3, U1.GND, Arduino1.GND
  N10: U2.pin4, U1.D52
  N11: U2.pin5, U1.D50
  N12: U2.pin6, U1.D51
  N13: U2.pin7, U1.D53
  N14: U3.pin1, J1.vcc
  N15: U3.pin4, U3.pin5, U3.pin6, U3.pin7, J1.gnd
  VIN: U1.VIN, Arduino1.VIN

custom parts:
  KEYPAD 4x3: KEYPAD matricial de 12 botones, 4 filas x 3 columnas
